// Logisim project Choice.circ as structural Verilog: 1 circuit, main circuit main
module main (
  input  [3:0] cpuout,
  input  [3:0] userout,
  input  who,
  output dmx0,
  output dmx1,
  output dmx2,
  output dmx3,
  output dmx4,
  output dmx5,
  output dmx6,
  output dmx7,
  output dmx8,
  output special
);

  wire demultiplexer_1_out0, demultiplexer_1_out10, demultiplexer_1_out11, demultiplexer_1_out12,
       demultiplexer_1_out13, demultiplexer_1_out14, demultiplexer_1_out15;
  wire [3:0] multiplexer_1_out;

  Multiplexer #(.width(4), .enable("false")) multiplexer_1 (
    .in0(cpuout), .in1(userout), .out(multiplexer_1_out), .sel(who));
  // Probe on multiplexer_1_out
  // Probe on 1'b1
  Demultiplexer #(.select(4), .disabled(0), .enable("false")) demultiplexer_1 (
    .out0(demultiplexer_1_out0), .out1(dmx0), .out2(dmx1), .out3(dmx2), .out4(dmx3), .out5(dmx4),
    .out6(dmx5), .out7(dmx6), .out8(dmx7), .out9(dmx8), .out10(demultiplexer_1_out10),
    .out11(demultiplexer_1_out11), .out12(demultiplexer_1_out12), .out13(demultiplexer_1_out13),
    .out14(demultiplexer_1_out14), .out15(demultiplexer_1_out15), .in(1'b1), .sel(multiplexer_1_out));
  // Probe on dmx0
  // Probe on dmx1
  // Probe on dmx2
  // Probe on dmx3
  or or_1 (special, demultiplexer_1_out0, demultiplexer_1_out10, demultiplexer_1_out11, demultiplexer_1_out12, demultiplexer_1_out13, demultiplexer_1_out14, demultiplexer_1_out15);
endmodule
