// Logisim project FullBoard.circ as structural Verilog: 1 circuit, main circuit main
module main (
  input  a0,
  input  a1,
  input  a2,
  input  a3,
  input  a4,
  input  a5,
  input  a6,
  input  a7,
  input  a8,
  output Exit
);

  wire and_1_out, and_2_out, and_3_out, and_4_out, and_5_out, and_6_out, and_7_out, and_8_out;

  and and_1 (and_1_out, a0, a1, a2);
  and and_2 (and_2_out, a0, a3, a6);
  and and_3 (and_3_out, a0, a4, a8);
  and and_4 (and_4_out, a1, a4, a7);
  and and_5 (and_5_out, a2, a5, a8);
  and and_6 (and_6_out, a2, a4, a6);
  and and_7 (and_7_out, a3, a4, a5);
  and and_8 (and_8_out, a6, a7, a8);
  or or_1 (Exit, and_1_out, and_2_out, and_3_out, and_4_out, and_5_out, and_6_out, and_7_out, and_8_out);
endmodule
