// Logisim project Start.circ as structural Verilog: 1 circuit, main circuit main
module main (
  input  used0,
  input  used1,
  input  used2,
  input  used3,
  input  used4,
  input  used5,
  input  used6,
  input  used7,
  input  used8,
  output start
);

  and and_1 (start, ~used0, ~used1, ~used2, ~used3, ~used4, ~used5, ~used6, ~used7, ~used8);  // AND_Gate
endmodule
