// Logisim project TTT_Epsilon.circ as structural Verilog: 1 circuit, main circuit main
module main (
  input  [3:0] in_1,
  input  [3:0] in_2,
  input  Execute
);

  wire CPUwin, dmx0, dmx1, dmx2, dmx3, dmx4, dmx5, dmx6, dmx7, dmx8, full, main_13_start, not_1_out,
       or_1_out, or_2_out, or_3_out, or_4_out, or_5_out, or_6_out, or_7_out, or_8_out, or_9_out, or_10_out,
       special, ts0, ts1, ts2, ts3, ts4, ts5, ts6, ts7, ts8, undriven, undriven_2, used0, used1, used2,
       used3, used4, used5, used6, used7, used8, UserWin, who, win;
  wire [3:0] bit_extender_1_out, bit_extender_2_out, bit_extender_3_out, counter_1_q, counter_2_q,
       counter_3_q, cpuout, to0, to1, to2, to3, to4, to5, to6, to7, to8, userout;

  assign bit_extender_1_out = {{3{1'b0}}, 1'b1};  // Bit_Extender bit_extender_1
  or or_1 (or_1_out, win, full);
  or or_2 (or_2_out, win, full);
  or or_3 (or_3_out, win, full);
  UserControl_main main_1 (.userin(in_1), .trigu(Execute), .userout(userout));
  Hex_Digit_Display hex_digit_display_1 (.value(counter_1_q));  // open: dp
  Counter #(.width(4), .max('hf), .trigger("falling")) counter_1 (
    .D(bit_extender_1_out), .Q(counter_1_q), .clk(UserWin));  // open: load, count, carry, clr
  Used_main main_2 (
    .trigu(Execute), .dmx0(dmx0), .win_full(or_1_out), .who(who), .truesingle(ts0), .used(used0),
    .trueoutput(to0));
  Used_main main_3 (
    .trigu(Execute), .dmx0(dmx3), .win_full(or_2_out), .who(who), .truesingle(ts3), .used(used3),
    .trueoutput(to3));
  Used_main main_4 (
    .trigu(Execute), .dmx0(dmx6), .win_full(or_3_out), .who(who), .truesingle(ts6), .used(used6),
    .trueoutput(to6));
  UserControl_main main_5 (.userin(in_2), .trigu(Execute), .userout(cpuout));
  Hex_Digit_Display hex_digit_display_2 (.value(to0));  // open: dp
  Hex_Digit_Display hex_digit_display_3 (.value(to3));  // open: dp
  Hex_Digit_Display hex_digit_display_4 (.value(to6));  // open: dp
  assign bit_extender_2_out = {{3{1'b0}}, 1'b1};  // Bit_Extender bit_extender_2
  or or_4 (or_4_out, win, full);
  or or_5 (or_5_out, win, full);
  or or_6 (or_6_out, win, full);
  // Probe on undriven
  // Probe on undriven
  Hex_Digit_Display hex_digit_display_5 (.value(counter_2_q));  // open: dp
  Counter #(.width(4), .max('hf), .trigger("falling")) counter_2 (
    .D(bit_extender_2_out), .Q(counter_2_q), .clk(CPUwin));  // open: load, count, carry, clr
  Used_main main_6 (
    .trigu(Execute), .dmx0(dmx1), .win_full(or_4_out), .who(who), .truesingle(ts1), .used(used1),
    .trueoutput(to1));
  Used_main main_7 (
    .trigu(Execute), .dmx0(dmx4), .win_full(or_5_out), .who(who), .truesingle(ts4), .used(used4),
    .trueoutput(to4));
  Used_main main_8 (
    .trigu(Execute), .dmx0(dmx7), .win_full(or_6_out), .who(who), .truesingle(ts7), .used(used7),
    .trueoutput(to7));
  Hex_Digit_Display hex_digit_display_6 (.value(to1));  // open: dp
  Hex_Digit_Display hex_digit_display_7 (.value(to4));  // open: dp
  Hex_Digit_Display hex_digit_display_8 (.value(to7));  // open: dp
  // Probe on undriven_2
  // Probe on undriven_2
  Hex_Digit_Display hex_digit_display_9 (.value(to2));  // open: dp
  Hex_Digit_Display hex_digit_display_10 (.value(to5));  // open: dp
  Hex_Digit_Display hex_digit_display_11 (.value(to8));  // open: dp
  or or_7 (or_7_out, win, full);
  or or_8 (or_8_out, win, full);
  or or_9 (or_9_out, win, full);
  Used_main main_9 (
    .trigu(Execute), .dmx0(dmx2), .win_full(or_7_out), .who(who), .truesingle(ts2), .used(used2),
    .trueoutput(to2));
  Used_main main_10 (
    .trigu(Execute), .dmx0(dmx5), .win_full(or_8_out), .who(who), .truesingle(ts5), .used(used5),
    .trueoutput(to5));
  Used_main main_11 (
    .trigu(Execute), .dmx0(dmx8), .win_full(or_9_out), .who(who), .truesingle(ts8), .used(used8),
    .trueoutput(to8));
  D_Flip_Flop #(.trigger("falling")) d_ff_1 (
    .Q(who), .preset(not_1_out), .reset(main_13_start));  // open: clk, D, Qn, en
  not not_1 (not_1_out, main_13_start);
  Choice_main main_12 (
    .cpuout(cpuout), .userout(userout), .who(who), .dmx0(dmx0), .dmx1(dmx1), .dmx2(dmx2), .dmx3(dmx3),
    .dmx4(dmx4), .dmx5(dmx5), .dmx6(dmx6), .dmx7(dmx7), .dmx8(dmx8), .special(special));
  Start_main main_13 (
    .used0(used0), .used1(used1), .used2(used2), .used3(used3), .used4(used4), .used5(used5), .used6(used6),
    .used7(used7), .used8(used8), .start(main_13_start));
  assign bit_extender_3_out = {{3{1'b0}}, 1'b1};  // Bit_Extender bit_extender_3
  Hex_Digit_Display hex_digit_display_12 (.value(counter_3_q));  // open: dp
  Counter #(.width(4), .max('hf), .trigger("falling")) counter_3 (
    .D(bit_extender_3_out), .Q(counter_3_q), .clk(or_10_out));  // open: load, count, carry, clr
  or or_10 (or_10_out, used8, used7, used6, used5, used4, used3, used2, used1, used0);
  WinCheck_main main_14 (
    .a0(ts0), .a1(ts1), .a2(ts2), .a3(ts3), .a4(ts4), .a5(ts5), .a6(ts6), .a7(ts7), .a8(ts8), .Exit(win),
    .UserWin(UserWin), .CPUwin(CPUwin));
  FullBoard_main main_15 (
    .a0(ts0), .a1(ts1), .a2(ts2), .a3(ts3), .a4(ts4), .a5(ts5), .a6(ts6), .a7(ts7), .a8(ts8), .Exit(full));

  // Other names for the same wires on the sheet: trigger = Execute

  // Notes on the sheet:
  //   send signal
  //   Turn Logic
  //   Push this to send choice to board
  //   User Input Logic
  //   Increments when user wins a game
  //   Memory Cells 
  //   Final Output
  //   _________________________________________
  //   __________________________________________
  //   Increments when CPU wins a game
  //   1 for user, 0 for computer
  //   turn logic IC
  //   <- Whats the choice
  //   Check For Win/Full Board
endmodule
