// Logisim project UserControl.circ as structural Verilog: 1 circuit, main circuit main
module main (
  input  [3:0] userin,
  input  trigu,
  output [3:0] userout
);

  D_Flip_Flop d_ff_1 (.clk(trigu), .D(userin[0]), .Q(userout[0]));  // open: Qn, preset, en, reset
  D_Flip_Flop d_ff_2 (.clk(trigu), .D(userin[1]), .Q(userout[1]));  // open: Qn, preset, en, reset
  D_Flip_Flop d_ff_3 (.clk(trigu), .D(userin[2]), .Q(userout[2]));  // open: Qn, preset, en, reset
  D_Flip_Flop d_ff_4 (.clk(trigu), .D(userin[3]), .Q(userout[3]));  // open: Qn, preset, en, reset
  // Probe on userout
endmodule
