// Logisim project WinCheck.circ as structural Verilog: 1 circuit, main circuit main
module main (
  input  a0,
  input  a1,
  input  a2,
  input  a3,
  input  a4,
  input  a5,
  input  a6,
  input  a7,
  input  a8,
  output Exit,
  output UserWin,
  output CPUwin
);

  wire and_1_out, and_2_out, and_3_out, and_4_out, and_5_out, and_6_out, and_7_out, and_8_out, and_9_out,
       and_10_out, and_11_out, and_12_out, and_13_out, and_14_out, and_15_out, and_16_out, and_17_out,
       and_18_out, and_19_out, and_20_out, and_21_out, and_22_out, and_23_out, and_24_out, and_25_out,
       and_26_out, and_27_out, and_28_out, and_29_out, and_30_out, and_31_out, and_32_out, not_1_out,
       not_2_out, not_3_out, not_4_out, not_5_out, not_6_out, not_7_out, not_8_out, not_9_out, not_10_out,
       not_11_out, not_12_out, not_13_out, not_14_out, not_15_out, not_16_out, not_17_out, not_18_out,
       not_19_out, not_20_out, not_21_out, not_22_out, not_23_out, not_24_out, not_25_out, not_26_out,
       not_27_out, not_28_out, not_29_out, not_30_out, not_31_out, not_32_out, not_33_out, not_34_out,
       not_35_out, not_36_out, not_37_out, not_38_out, not_39_out, not_40_out, not_41_out, not_42_out,
       not_43_out, not_44_out, not_45_out, not_46_out, not_47_out, not_48_out;

  not not_1 (not_1_out, a0);
  not not_2 (not_2_out, a1);
  not not_3 (not_3_out, a2);
  not not_4 (not_4_out, a0);
  not not_5 (not_5_out, a3);
  not not_6 (not_6_out, a6);
  not not_7 (not_7_out, a0);
  not not_8 (not_8_out, a4);
  not not_9 (not_9_out, a8);
  not not_10 (not_10_out, a1);
  not not_11 (not_11_out, a4);
  not not_12 (not_12_out, a7);
  not not_13 (not_13_out, a2);
  not not_14 (not_14_out, a5);
  not not_15 (not_15_out, a8);
  not not_16 (not_16_out, a2);
  not not_17 (not_17_out, a4);
  not not_18 (not_18_out, a6);
  not not_19 (not_19_out, a3);
  not not_20 (not_20_out, a4);
  not not_21 (not_21_out, a5);
  not not_22 (not_22_out, a6);
  not not_23 (not_23_out, a7);
  not not_24 (not_24_out, a8);
  and and_1 (and_1_out, a0, a1, a2);
  and and_2 (and_2_out, a0, a3, a6);
  and and_3 (and_3_out, a0, a4, a8);
  and and_4 (and_4_out, a1, a4, a7);
  and and_5 (and_5_out, a2, a5, a8);
  and and_6 (and_6_out, a2, a4, a6);
  and and_7 (and_7_out, a3, a4, a5);
  and and_8 (and_8_out, a6, a7, a8);
  not not_25 (not_25_out, a0);
  not not_26 (not_26_out, a1);
  not not_27 (not_27_out, a2);
  not not_28 (not_28_out, a0);
  not not_29 (not_29_out, a3);
  not not_30 (not_30_out, a6);
  not not_31 (not_31_out, a0);
  not not_32 (not_32_out, a4);
  not not_33 (not_33_out, a8);
  not not_34 (not_34_out, a1);
  not not_35 (not_35_out, a4);
  not not_36 (not_36_out, a7);
  not not_37 (not_37_out, a2);
  not not_38 (not_38_out, a5);
  not not_39 (not_39_out, a8);
  not not_40 (not_40_out, a2);
  not not_41 (not_41_out, a4);
  not not_42 (not_42_out, a6);
  not not_43 (not_43_out, a3);
  not not_44 (not_44_out, a4);
  not not_45 (not_45_out, a5);
  not not_46 (not_46_out, a6);
  not not_47 (not_47_out, a7);
  not not_48 (not_48_out, a8);
  and and_9 (and_9_out, a0, a1, a2);
  and and_10 (and_10_out, a0, a3, a6);
  and and_11 (and_11_out, a0, a4, a8);
  and and_12 (and_12_out, a1, a4, a7);
  and and_13 (and_13_out, a2, a5, a8);
  and and_14 (and_14_out, a2, a4, a6);
  and and_15 (and_15_out, a3, a4, a5);
  and and_16 (and_16_out, a6, a7, a8);
  and and_17 (and_17_out, not_1_out, not_2_out, not_3_out);
  and and_18 (and_18_out, not_4_out, not_5_out, not_6_out);
  and and_19 (and_19_out, not_7_out, not_8_out, not_9_out);
  and and_20 (and_20_out, not_10_out, not_11_out, not_12_out);
  and and_21 (and_21_out, not_13_out, not_14_out, not_15_out);
  and and_22 (and_22_out, not_16_out, not_17_out, not_18_out);
  and and_23 (and_23_out, not_19_out, not_20_out, not_21_out);
  and and_24 (and_24_out, not_22_out, not_23_out, not_24_out);
  or or_1 (UserWin, and_1_out, and_2_out, and_3_out, and_4_out, and_5_out, and_6_out, and_7_out, and_8_out);
  and and_25 (and_25_out, not_25_out, not_26_out, not_27_out);
  and and_26 (and_26_out, not_28_out, not_29_out, not_30_out);
  and and_27 (and_27_out, not_31_out, not_32_out, not_33_out);
  and and_28 (and_28_out, not_34_out, not_35_out, not_36_out);
  and and_29 (and_29_out, not_37_out, not_38_out, not_39_out);
  and and_30 (and_30_out, not_40_out, not_41_out, not_42_out);
  and and_31 (and_31_out, not_43_out, not_44_out, not_45_out);
  and and_32 (and_32_out, not_46_out, not_47_out, not_48_out);
  or or_2 (Exit, and_9_out, and_10_out, and_11_out, and_12_out, and_13_out, and_14_out, and_15_out, and_16_out, and_17_out, and_18_out, and_19_out, and_20_out, and_21_out, and_22_out, and_23_out, and_24_out);
  or or_3 (CPUwin, and_25_out, and_26_out, and_27_out, and_28_out, and_29_out, and_30_out, and_31_out, and_32_out);
endmodule
