// Logisim project TTT_Epsilon.circ as structural Verilog: 1 circuit, main circuit main
module main (
  input  [3:0] in_1,
  input  [3:0] in_2,
  input  in_3,
  input  in_4
);

  wire dmx0, dmx1, dmx2, dmx3, dmx4, dmx5, dmx6, dmx7, dmx8, special, undriven, undriven_2, used0, used1,
       used2, used3, used4, used5, used6, used7, used8;
  wire [3:0] to0, to1, to2, to3, to4, to5, to6, to7, to8, userout;

  UserControl_main main_1 (.userin(in_1), .trigu(in_4), .userout(userout));
  Used_main main_2 (.trigu(in_4), .dmx0(dmx0), .who(in_3), .used(used0), .trueoutput(to0));
  Used_main main_3 (.trigu(in_4), .dmx0(dmx3), .who(in_3), .used(used3), .trueoutput(to3));
  Used_main main_4 (.trigu(in_4), .dmx0(dmx6), .who(in_3), .used(used6), .trueoutput(to6));
  Used_main main_5 (.trigu(in_4), .dmx0(dmx1), .who(in_3), .used(used1), .trueoutput(to1));
  Used_main main_6 (.trigu(in_4), .dmx0(dmx4), .who(in_3), .used(used4), .trueoutput(to4));
  Used_main main_7 (.trigu(in_4), .dmx0(dmx7), .who(in_3), .used(used7), .trueoutput(to7));
  Choice_main main_8 (
    .cpuout(in_2), .userout(userout), .who(in_3), .dmx0(dmx0), .dmx1(dmx1), .dmx2(dmx2), .dmx3(dmx3),
    .dmx4(dmx4), .dmx5(dmx5), .dmx6(dmx6), .dmx7(dmx7), .dmx8(dmx8), .special(special));
  Used_main main_9 (.trigu(in_4), .dmx0(dmx2), .who(in_3), .used(used2), .trueoutput(to2));
  Used_main main_10 (.trigu(in_4), .dmx0(dmx5), .who(in_3), .used(used5), .trueoutput(to5));
  Used_main main_11 (.trigu(in_4), .dmx0(dmx8), .who(in_3), .used(used8), .trueoutput(to8));
  Hex_Digit_Display hex_digit_display_1 (.value(to0));  // open: dp
  Hex_Digit_Display hex_digit_display_2 (.value(to3));  // open: dp
  Hex_Digit_Display hex_digit_display_3 (.value(to6));  // open: dp
  // Probe on undriven
  // Probe on undriven
  Hex_Digit_Display hex_digit_display_4 (.value(to1));  // open: dp
  Hex_Digit_Display hex_digit_display_5 (.value(to4));  // open: dp
  Hex_Digit_Display hex_digit_display_6 (.value(to7));  // open: dp
  // Probe on undriven_2
  // Probe on undriven_2
  Hex_Digit_Display hex_digit_display_7 (.value(to2));  // open: dp
  Hex_Digit_Display hex_digit_display_8 (.value(to5));  // open: dp
  Hex_Digit_Display hex_digit_display_9 (.value(to8));  // open: dp

  // Other names for the same wires on the sheet: cpuout[3:0] = in_2; trigu = in_4; who = in_3

  // Notes on the sheet:
  //   send signal
  //   User Input Logic
  //   Turn Logic
  //   Memory Cells 
  //   <- Whats the choice
  //   Final Output
  //   _________________________________________
  //   __________________________________________
  //   Used?
endmodule
