// Logisim project Used.circ as structural Verilog: 1 circuit, main circuit main
module main (
  input  who,
  input  trigu,
  input  dmx0,
  input  win_full,
  output used,
  output [3:0] trueoutput,
  output truesingle
);

  wire and_1_out, and_2_out, d_ff_2_q, not_1_out, not_2_out, or_1_out;
  wire [3:0] initalout;

  and and_1 (and_1_out, who, trigu, dmx0);
  and and_2 (and_2_out, ~who, dmx0);  // AND_Gate
  or or_1 (or_1_out, and_2_out, and_1_out);
  not not_1 (not_1_out, used);
  D_Flip_Flop d_ff_1 (.clk(or_1_out), .D(dmx0), .Q(used), .en(not_1_out), .reset(win_full));  // open: Qn, preset
  Transistor #(.\type ("n"), .width(4)) transistor_1 (.in(initalout), .out(trueoutput), .gate(used));
  BitSelector #(.width(4)) bitselector_1 (.in(trueoutput), .out(truesingle), .sel(2'b00));
  Bit_Extender #(.in_width(4)) bit_extender_1 ();  // open: in, out
  D_Flip_Flop d_ff_2 (.clk(used), .D(who), .Q(d_ff_2_q), .en(not_2_out));  // open: Qn, preset, reset
  not not_2 (not_2_out, used);
  assign initalout = {{3{1'b0}}, d_ff_2_q};  // Bit_Extender bit_extender_2
endmodule
